// Logisim project Basic Computer.circ as structural Verilog: 30 circuits, main circuit main
// I
module main (
  input  [7:0] INPR,
  output [15:0] out_2,
  output [15:0] out_3,
  output [15:0] out_4,
  output [15:0] out_5,
  output [15:0] out_6,
  output [15:0] out_7,
  output [15:0] out_8,
  output [7:0] out_9
);

  wire AC_CTRL_clr, AC_CTRL_inc, AR_CTRL_clr, AR_CTRL_inc, AR_CTRL_ld, CLK, clock_1_out, DR_CTRL_inc,
       DR_CTRL_ld, E, E_out, FGI, FGO, I, IEN, ir_controller_1_ld, memory_1_read, memory_1_write, not_1_out,
       not_2_out, or_1_out, OUTR_CTRL_ld, PC_CTRL_clr, PC_CTRL_inc, PC_CTRL_ld, R, S,
       sc_clear_controller_1_sc_clr, TR_CTRL_clr, TR_CTRL_inc, TR_CTRL_ld;
  wire [2:0] BUS_CTRL_select;
  wire [3:0] SC;
  wire [6:0] AC_CTRL_and;
  wire [7:0] inpr_1_out_1;
  wire [15:0] bus_1_select, ram_1_data;

  Clock clock_1 (.out(clock_1_out));
  INPR inpr_1 (.out_1(inpr_1_out_1));
  not not_1 (not_1_out, S);
  SC_Clear_Controller sc_clear_controller_1 (.I(I), .R(R), .IR(out_7), .Seq(SC), .SC_CLR(sc_clear_controller_1_sc_clr));
  S_Controller s_controller_1 (.I(I), .IR(out_7), .Seq(SC), .S(S), .CLK(CLK));
  and and_1 (CLK, clock_1_out, not_1_out);
  not not_2 (not_2_out, sc_clear_controller_1_sc_clr);
  IEN_Controller ien_controller_1 (.I(I), .R(R), .IR(out_7), .Seq(SC), .IEN(IEN), .CLK(CLK));
  AC_Controller AC_CTRL (
    .I(I), .IR(out_7), .Seq(SC), .AND(AC_CTRL_and[0]), .ADD(AC_CTRL_and[1]), .DR(AC_CTRL_and[2]),
    .INC(AC_CTRL_inc), .INPR(AC_CTRL_and[3]), .COM(AC_CTRL_and[4]), .CLR(AC_CTRL_clr), .SHR(AC_CTRL_and[5]),
    .SHL(AC_CTRL_and[6]));
  Counter #(.width(4), .max('hf)) counter_1 (
    .load(sc_clear_controller_1_sc_clr), .D(4'b0000), .count(not_2_out), .Q(SC), .clk(CLK));  // open: carry, clr
  ALU_16_bits alu_16_bits_1 (
    .E_in(E), .INPR(inpr_1_out_1), .AC(out_6), .DR(out_4), .AND(AC_CTRL_and[0]), .ADD(AC_CTRL_and[1]),
    .OUTPUT(out_5), .DR_2(AC_CTRL_and[2]), .INPR_2(AC_CTRL_and[3]), .COM(AC_CTRL_and[4]),
    .SHR(AC_CTRL_and[5]), .SHL(AC_CTRL_and[6]), .E_out(E_out));
  OUTR_Controller OUTR_CTRL (.I(I), .IR(out_7), .Seq(SC), .LD(OUTR_CTRL_ld));
  OUTR outr_1 (.INPUT(bus_1_select), .OUTPUT(out_9), .LD(OUTR_CTRL_ld), .CLK(CLK));
  or or_1 (or_1_out, AC_CTRL_and[0], AC_CTRL_and[1], AC_CTRL_and[2], AC_CTRL_and[3], AC_CTRL_and[4], AC_CTRL_and[5], AC_CTRL_and[6]);
  R_Controller r_controller_1 (.IEN(IEN), .FGO(FGO), .FGI(FGI), .Seq(SC), .R(R), .CLK(CLK));
  FGI_Controller fgi_controller_1 (.INPUT(INPR), .I(I), .IR(out_7), .Seq(SC), .CLK(CLK), .FGI(FGI));
  E_Controller e_controller_1 (.E_out(E_out), .I(I), .IR(out_7), .Seq(SC), .AC(out_6), .E(E), .in_1(CLK));
  Memory memory_1 (.Write(memory_1_write), .Read(memory_1_read), .I(I), .R(R), .IR(out_7), .Seq(SC));
  AR_Controller AR_CTRL (.I(I), .R(R), .IR(out_7), .Seq(SC), .LD(AR_CTRL_ld), .INC(AR_CTRL_inc), .CLR(AR_CTRL_clr));
  PC_Controller PC_CTRL (
    .AC(out_6), .FGO(FGO), .FGI(FGI), .E(E), .I(I), .R(R), .IR(out_7), .DR(out_4), .Seq(SC), .LD(PC_CTRL_ld),
    .CLR(PC_CTRL_clr), .INC(PC_CTRL_inc));
  IR_Controller ir_controller_1 (.R(R), .Seq(SC), .LD(ir_controller_1_ld));
  TR_Controller TR_CTRL (.R(R), .Seq(SC), .LD(TR_CTRL_ld), .INC(TR_CTRL_inc), .CLR(TR_CTRL_clr));
  RAM #(.addrWidth(12), .dataWidth(16), .bus("separate")) ram_1 (
    .addr(out_2[11:0]), .din(bus_1_select), .data(ram_1_data), .str(memory_1_write), .clk(CLK),
    .ld(memory_1_read));  // open: sel, clr
  DR_Controller DR_CTRL (.IR(out_7), .Seq(SC), .LD(DR_CTRL_ld), .INC(DR_CTRL_inc));
  AR ar_1 (.INPUT(bus_1_select), .OUTPUT(out_2), .CLR(AR_CTRL_clr), .LD(AR_CTRL_ld), .INC(AR_CTRL_inc), .CLK(CLK));
  PC pc_1 (.INPUT(bus_1_select), .OUTPUT(out_3), .CLR(PC_CTRL_clr), .LD(PC_CTRL_ld), .INC(PC_CTRL_inc), .CLK(CLK));
  DR dr_1 (.INPUT(bus_1_select), .OUTPUT(out_4), .LD(DR_CTRL_ld), .INC(DR_CTRL_inc), .CLK(CLK));  // open: CLR
  AC ac_1 (.INPUT(out_5), .OUTPUT(out_6), .CLR(AC_CTRL_clr), .LD(or_1_out), .INC(AC_CTRL_inc), .CLK(CLK));
  IR ir_1 (.INPUT(bus_1_select), .OUTPUT(out_7), .LD(ir_controller_1_ld), .CLK(CLK));
  TR tr_1 (.INPUT(bus_1_select), .OUTPUT(out_8), .CLR(TR_CTRL_clr), .LD(TR_CTRL_ld), .INC(TR_CTRL_inc), .CLK(CLK));
  I_Controller i_controller_1 (.IR_15(out_7[15]), .R(R), .Seq(SC), .I(I), .CLK(CLK));
  FGO_Controller fgo_controller_1 (.I(I), .IR(out_7), .Seq(SC), .FGO(FGO), .CLK(CLK));
  BUS_Controller BUS_CTRL (.I(I), .R(R), .IR(out_7), .Seq(SC), .SELECT(BUS_CTRL_select));
  BUS bus_1 (
    .AR(out_2), .PC(out_3), .DR(out_4), .AC(out_6), .IR(out_7), .TR(out_8), .S2(BUS_CTRL_select[2]),
    .Memory(ram_1_data), .SELECT(bus_1_select), .S0(BUS_CTRL_select[0]), .S1(BUS_CTRL_select[1]));

  // Other names for the same wires on the sheet: AC[15:0] = out_6; AR[15:0] = out_2; DR[15:0] = out_4;
  //   IR[15:0] = out_7; IR_15 = out_7[15]; PC[15:0] = out_3; TR[15:0] = out_8
endmodule

module ALU_UNIT (
  input  [6:0] INPUT_CONTROL_GATES,
  input  AC_i,
  input  DR_i,
  input  C_i,
  input  INPR_i,
  input  AC_i_1,
  input  AC_i_1_2,
  output C_i_1,
  output I_i
);

  wire ADD_out, AND_out, COM_out, DR_out, fa_1_s_i, INPR_out, not_1_out, SHL_out, SHR_out;

  FA fa_1 (.C_i(C_i), .A_i(AC_i), .B_i(DR_i), .S_i(fa_1_s_i), .C_i_1(C_i_1));
  not not_1 (not_1_out, AC_i);
  and AND (AND_out, INPUT_CONTROL_GATES[6], AC_i, DR_i);
  and ADD (ADD_out, INPUT_CONTROL_GATES[5], fa_1_s_i);
  and DR (DR_out, INPUT_CONTROL_GATES[4], DR_i);
  and INPR (INPR_out, INPUT_CONTROL_GATES[3], INPR_i);
  and COM (COM_out, INPUT_CONTROL_GATES[2], not_1_out);
  and SHR (SHR_out, INPUT_CONTROL_GATES[1], AC_i_1);
  and SHL (SHL_out, INPUT_CONTROL_GATES[0], AC_i_1_2);
  or u_I_i (I_i, AND_out, ADD_out, DR_out, INPR_out, COM_out, SHR_out, SHL_out);
endmodule

// ALU
module ALU_16_bits (
  input  E_in,
  input  [7:0] INPR,
  input  [15:0] AC,
  input  [15:0] DR,
  input  AND,
  input  ADD,
  input  DR_2,
  input  INPR_2,
  input  COM,
  input  SHR,
  input  SHL,
  output E_out,
  output [15:0] OUTPUT
);

  wire alu_unit_1_c_i_1, alu_unit_2_c_i_1, alu_unit_3_c_i_1, alu_unit_4_c_i_1, alu_unit_5_c_i_1,
       alu_unit_6_c_i_1, alu_unit_7_c_i_1, alu_unit_8_c_i_1, alu_unit_9_c_i_1, alu_unit_10_c_i_1,
       alu_unit_11_c_i_1, alu_unit_12_c_i_1, alu_unit_13_c_i_1, alu_unit_14_c_i_1, alu_unit_15_c_i_1,
       and_1_out, and_2_out, and_3_out, and_4_out, C_16, nor_1_out;

  nor nor_1 (nor_1_out, SHR, ADD, SHL);
  and and_1 (and_1_out, AC[15], SHL);
  and and_2 (and_2_out, AC[0], SHR);
  and and_3 (and_3_out, ADD, C_16);
  and and_4 (and_4_out, E_in, nor_1_out);
  or or_1 (E_out, and_1_out, and_2_out, and_3_out, and_4_out);
  ALU_UNIT alu_unit_1 (
    .INPUT_CONTROL_GATES({AND, ADD, DR_2, INPR_2, COM, SHR, SHL}), .C_i_1(alu_unit_1_c_i_1),
    .INPR_i(INPR[0]), .AC_i_1(AC[1]), .AC_i_1_2(E_in), .DR_i(DR[0]), .AC_i(AC[0]), .C_i(1'b0), .I_i(OUTPUT[0]));
  ALU_UNIT alu_unit_2 (
    .INPUT_CONTROL_GATES({AND, ADD, DR_2, INPR_2, COM, SHR, SHL}), .C_i_1(alu_unit_2_c_i_1),
    .INPR_i(INPR[1]), .AC_i_1(AC[2]), .AC_i_1_2(AC[0]), .DR_i(DR[1]), .AC_i(AC[1]), .C_i(alu_unit_1_c_i_1),
    .I_i(OUTPUT[1]));
  ALU_UNIT alu_unit_3 (
    .INPUT_CONTROL_GATES({AND, ADD, DR_2, INPR_2, COM, SHR, SHL}), .C_i_1(alu_unit_3_c_i_1),
    .INPR_i(INPR[2]), .AC_i_1(AC[3]), .AC_i_1_2(AC[1]), .DR_i(DR[2]), .AC_i(AC[2]), .C_i(alu_unit_2_c_i_1),
    .I_i(OUTPUT[2]));
  ALU_UNIT alu_unit_4 (
    .INPUT_CONTROL_GATES({AND, ADD, DR_2, INPR_2, COM, SHR, SHL}), .C_i_1(alu_unit_4_c_i_1),
    .INPR_i(INPR[3]), .AC_i_1(AC[4]), .AC_i_1_2(AC[2]), .DR_i(DR[3]), .AC_i(AC[3]), .C_i(alu_unit_3_c_i_1),
    .I_i(OUTPUT[3]));
  ALU_UNIT alu_unit_5 (
    .INPUT_CONTROL_GATES({AND, ADD, DR_2, INPR_2, COM, SHR, SHL}), .C_i_1(alu_unit_5_c_i_1),
    .INPR_i(INPR[4]), .AC_i_1(AC[5]), .AC_i_1_2(AC[3]), .DR_i(DR[4]), .AC_i(AC[4]), .C_i(alu_unit_4_c_i_1),
    .I_i(OUTPUT[4]));
  ALU_UNIT alu_unit_6 (
    .INPUT_CONTROL_GATES({AND, ADD, DR_2, INPR_2, COM, SHR, SHL}), .C_i_1(alu_unit_6_c_i_1),
    .INPR_i(INPR[5]), .AC_i_1(AC[6]), .AC_i_1_2(AC[4]), .DR_i(DR[5]), .AC_i(AC[5]), .C_i(alu_unit_5_c_i_1),
    .I_i(OUTPUT[5]));
  ALU_UNIT alu_unit_7 (
    .INPUT_CONTROL_GATES({AND, ADD, DR_2, INPR_2, COM, SHR, SHL}), .C_i_1(alu_unit_7_c_i_1),
    .INPR_i(INPR[6]), .AC_i_1(AC[7]), .AC_i_1_2(AC[5]), .DR_i(DR[6]), .AC_i(AC[6]), .C_i(alu_unit_6_c_i_1),
    .I_i(OUTPUT[6]));
  ALU_UNIT alu_unit_8 (
    .INPUT_CONTROL_GATES({AND, ADD, DR_2, INPR_2, COM, SHR, SHL}), .C_i_1(alu_unit_8_c_i_1),
    .INPR_i(INPR[7]), .AC_i_1(AC[8]), .AC_i_1_2(AC[6]), .DR_i(DR[7]), .AC_i(AC[7]), .C_i(alu_unit_7_c_i_1),
    .I_i(OUTPUT[7]));
  ALU_UNIT alu_unit_9 (
    .INPUT_CONTROL_GATES({AND, ADD, DR_2, INPR_2, COM, SHR, SHL}), .C_i_1(alu_unit_9_c_i_1), .INPR_i(1'b0),
    .AC_i_1(AC[9]), .AC_i_1_2(AC[7]), .DR_i(DR[8]), .AC_i(AC[8]), .C_i(alu_unit_8_c_i_1), .I_i(OUTPUT[8]));
  ALU_UNIT alu_unit_10 (
    .INPUT_CONTROL_GATES({AND, ADD, DR_2, INPR_2, COM, SHR, SHL}), .C_i_1(alu_unit_10_c_i_1), .INPR_i(1'b0),
    .AC_i_1(AC[10]), .AC_i_1_2(AC[8]), .DR_i(DR[9]), .AC_i(AC[9]), .C_i(alu_unit_9_c_i_1), .I_i(OUTPUT[9]));
  ALU_UNIT alu_unit_11 (
    .INPUT_CONTROL_GATES({AND, ADD, DR_2, INPR_2, COM, SHR, SHL}), .C_i_1(alu_unit_11_c_i_1), .INPR_i(1'b0),
    .AC_i_1(AC[11]), .AC_i_1_2(AC[9]), .DR_i(DR[10]), .AC_i(AC[10]), .C_i(alu_unit_10_c_i_1), .I_i(OUTPUT[10]));
  ALU_UNIT alu_unit_12 (
    .INPUT_CONTROL_GATES({AND, ADD, DR_2, INPR_2, COM, SHR, SHL}), .C_i_1(alu_unit_12_c_i_1), .INPR_i(1'b0),
    .AC_i_1(AC[12]), .AC_i_1_2(AC[10]), .DR_i(DR[11]), .AC_i(AC[11]), .C_i(alu_unit_11_c_i_1),
    .I_i(OUTPUT[11]));
  ALU_UNIT alu_unit_13 (
    .INPUT_CONTROL_GATES({AND, ADD, DR_2, INPR_2, COM, SHR, SHL}), .C_i_1(alu_unit_13_c_i_1), .INPR_i(1'b0),
    .AC_i_1(AC[13]), .AC_i_1_2(AC[11]), .DR_i(DR[12]), .AC_i(AC[12]), .C_i(alu_unit_12_c_i_1),
    .I_i(OUTPUT[12]));
  ALU_UNIT alu_unit_14 (
    .INPUT_CONTROL_GATES({AND, ADD, DR_2, INPR_2, COM, SHR, SHL}), .C_i_1(alu_unit_14_c_i_1), .INPR_i(1'b0),
    .AC_i_1(AC[14]), .AC_i_1_2(AC[12]), .DR_i(DR[13]), .AC_i(AC[13]), .C_i(alu_unit_13_c_i_1),
    .I_i(OUTPUT[13]));
  ALU_UNIT alu_unit_15 (
    .INPUT_CONTROL_GATES({AND, ADD, DR_2, INPR_2, COM, SHR, SHL}), .C_i_1(alu_unit_15_c_i_1), .INPR_i(1'b0),
    .AC_i_1(AC[15]), .AC_i_1_2(AC[13]), .DR_i(DR[14]), .AC_i(AC[14]), .C_i(alu_unit_14_c_i_1),
    .I_i(OUTPUT[14]));
  ALU_UNIT alu_unit_16 (
    .INPUT_CONTROL_GATES({AND, ADD, DR_2, INPR_2, COM, SHR, SHL}), .C_i_1(C_16), .INPR_i(1'b0),
    .AC_i_1(E_in), .AC_i_1_2(AC[14]), .DR_i(DR[15]), .AC_i(AC[15]), .C_i(alu_unit_15_c_i_1), .I_i(OUTPUT[15]));

  // Other names for the same wires on the sheet: AC_0 = AC[0]; AC_1 = AC[1]; AC_2 = AC[2]; AC_3 = AC[3]; AC_4 = AC[4];
  //   AC_5 = AC[5]; AC_6 = AC[6]; AC_7 = AC[7]; AC_8 = AC[8]; AC_9 = AC[9]; AC_10 = AC[10]; AC_11 = AC[11];
  //   AC_12 = AC[12]; AC_13 = AC[13]; AC_14 = AC[14]; AC_15 = AC[15];
  //   Control_Gates[6:0] = {AND, ADD, DR_2, INPR_2, COM, SHR, SHL}; INPR_t = INPR_2; DR_t = DR_2; DR_0 = DR[0];
  //   DR_1 = DR[1]; DR_2_t = DR[2]; DR_3 = DR[3]; DR_4 = DR[4]; DR_5 = DR[5]; DR_6 = DR[6]; DR_7 = DR[7];
  //   DR_8 = DR[8]; DR_9 = DR[9]; DR_10 = DR[10]; DR_11 = DR[11]; DR_12 = DR[12]; DR_13 = DR[13]; DR_14 = DR[14];
  //   DR_15 = DR[15]; IN0 = INPR[0]; IN1 = INPR[1]; IN2 = INPR[2]; IN3 = INPR[3]; IN4 = INPR[4]; IN5 = INPR[5];
  //   IN6 = INPR[6]; IN7 = INPR[7]; I_0 = OUTPUT[0]; I_1 = OUTPUT[1]; I_2 = OUTPUT[2]; I_3 = OUTPUT[3];
  //   I_4 = OUTPUT[4]; I_5 = OUTPUT[5]; I_6 = OUTPUT[6]; I_7 = OUTPUT[7]; I_8 = OUTPUT[8]; I_9 = OUTPUT[9];
  //   I_10 = OUTPUT[10]; I_11 = OUTPUT[11]; I_12 = OUTPUT[12]; I_13 = OUTPUT[13]; I_14 = OUTPUT[14];
  //   I_15 = OUTPUT[15]
endmodule

module FA (
  input  C_i,
  input  A_i,
  input  B_i,
  output S_i,
  output C_i_1
);

  wire and_1_out, and_2_out, xor_1_out;

  xor xor_1 (xor_1_out, A_i, B_i);
  and and_1 (and_1_out, A_i, B_i);
  xor xor_2 (S_i, C_i, xor_1_out);
  and and_2 (and_2_out, C_i, xor_1_out);
  or or_1 (C_i_1, and_2_out, and_1_out);
endmodule

module BUS (
  input  [15:0] AR,
  input  [15:0] PC,
  input  [15:0] DR,
  input  [15:0] AC,
  input  [15:0] IR,
  input  [15:0] TR,
  input  S2,
  input  S0,
  input  S1,
  input  [15:0] Memory,
  output [15:0] SELECT
);

  Multiplexer #(.select(3), .width(16)) multiplexer_1 (
    .in1(AR), .in2(PC), .in3(DR), .in4(AC), .in5(IR), .in6(TR), .in7(Memory), .out(SELECT), .sel({S2, S1, S0}));  // open: in0, en
endmodule

module AC (
  input  LD,
  input  [15:0] INPUT,
  input  INC,
  input  CLR,
  input  CLK,
  output [15:0] OUTPUT
);

  Counter #(.width(16), .max('hffff)) counter_1 (
    .load(LD), .D(INPUT), .count(INC), .Q(OUTPUT), .clk(CLK), .clr(CLR));  // open: carry
endmodule

module AC_Controller (
  input  I,
  input  [15:0] IR,
  input  [3:0] Seq,
  output AND,
  output ADD,
  output DR,
  output INC,
  output INPR,
  output COM,
  output CLR,
  output SHR,
  output SHL
);

  wire D0, D1, D2, D3, D4, D5, D6, D7, not_1_out, p, r, T0, T1, T2, T3, T4, T5, T6, T7, T8, T9, T10, T11,
       T12, T13, T14, T15;

  not not_1 (not_1_out, I);
  Decoder #(.select(4)) decoder_1 (
    .out0(T0), .out1(T1), .out2(T2), .out3(T3), .out4(T4), .out5(T5), .out6(T6), .out7(T7), .out8(T8),
    .out9(T9), .out10(T10), .out11(T11), .out12(T12), .out13(T13), .out14(T14), .out15(T15), .sel(Seq),
    .en(1'b1));
  and u_AND (AND, D0, T5);
  and u_ADD (ADD, T5, D1);
  and u_DR (DR, T5, D2);
  and u_INPR (INPR, p, IR[11]);
  and u_COM (COM, r, IR[9]);
  and u_SHR (SHR, r, IR[7]);
  and u_SHL (SHL, r, IR[6]);
  and and_2 (r, D7, not_1_out, T3);
  and and_3 (p, D7, I, T3);
  Decoder #(.select(3)) decoder_2 (
    .out0(D0), .out1(D1), .out2(D2), .out3(D3), .out4(D4), .out5(D5), .out6(D6), .out7(D7), .sel(IR[14:12]));  // open: en
  and and_4 (INC, r, IR[5]);
  and and_5 (CLR, r, IR[11]);

  // Other names for the same wires on the sheet: B0 = IR[0]; B1 = IR[1]; B2 = IR[2]; B3 = IR[3]; B4 = IR[4];
  //   B5 = IR[5]; B6 = IR[6]; B7 = IR[7]; B8 = IR[8]; B9 = IR[9]; B10 = IR[10]; B11 = IR[11]; IR_15 = IR[15]
endmodule

module AR (
  input  LD,
  input  [15:0] INPUT,
  input  INC,
  input  CLR,
  input  CLK,
  output [15:0] OUTPUT
);

  Counter #(.width(12), .max('hfff)) counter_1 (
    .load(LD), .D(INPUT[11:0]), .count(INC), .Q(OUTPUT[11:0]), .clk(CLK), .clr(CLR));  // open: carry

  assign OUTPUT[15:12] = 4'b0000;
endmodule

module AR_Controller (
  input  I,
  input  R,
  input  [15:0] IR,
  input  [3:0] Seq,
  output LD,
  output INC,
  output CLR
);

  wire and_1_out, and_2_out, and_3_out, D0, D1, D2, D3, D4, D5, D6, D7, not_1_out, not_2_out, T0, T1, T2, T3,
       T4, T5, T6, T7, T8, T9, T10, T11, T12, T13, T14, T15;

  and and_1 (and_1_out, not_1_out, I, T3);
  not not_1 (not_1_out, D7);
  or or_1 (LD, and_1_out, and_2_out, and_3_out);
  and and_2 (and_2_out, not_2_out, T2);
  not not_2 (not_2_out, R);
  Decoder #(.select(4)) decoder_1 (
    .out0(T0), .out1(T1), .out2(T2), .out3(T3), .out4(T4), .out5(T5), .out6(T6), .out7(T7), .out8(T8),
    .out9(T9), .out10(T10), .out11(T11), .out12(T12), .out13(T13), .out14(T14), .out15(T15), .sel(Seq),
    .en(1'b1));
  and and_3 (and_3_out, not_2_out, T0);
  and and_4 (INC, D5, T4);
  and and_5 (CLR, R, T0);
  Decoder #(.select(3)) decoder_2 (
    .out0(D0), .out1(D1), .out2(D2), .out3(D3), .out4(D4), .out5(D5), .out6(D6), .out7(D7), .sel(IR[14:12]));  // open: en

  // Other names for the same wires on the sheet: B0 = IR[0]; B1 = IR[1]; B2 = IR[2]; B3 = IR[3]; B4 = IR[4];
  //   B5 = IR[5]; B6 = IR[6]; B7 = IR[7]; B8 = IR[8]; B9 = IR[9]; B10 = IR[10]; B11 = IR[11]; IR_15 = IR[15]
endmodule

module PC (
  input  LD,
  input  [15:0] INPUT,
  input  INC,
  input  CLR,
  input  CLK,
  output [15:0] OUTPUT
);

  Counter #(.width(12), .max('hfff)) counter_1 (
    .load(LD), .D(INPUT[11:0]), .count(INC), .Q(OUTPUT[11:0]), .clk(CLK), .clr(CLR));  // open: carry

  assign OUTPUT[15:12] = 4'b0000;
endmodule

module PC_Controller (
  input  [15:0] AC,
  input  FGO,
  input  FGI,
  input  E,
  input  I,
  input  R,
  input  [15:0] IR,
  input  [15:0] DR,
  input  [3:0] Seq,
  output LD,
  output CLR,
  output INC
);

  wire AC_t, and_2_out, and_3_out, and_5_out, and_6_out, and_7_out, and_8_out, and_9_out, and_10_out,
       and_11_out, and_12_out, and_13_out, D0, D1, D2, D3, D4, D5, D6, D7, DR_t, not_1_out, not_2_out,
       not_3_out, not_4_out, not_5_out, not_6_out, p, r_t, T0, T1, T2, T3, T4, T5, T6, T7, T8, T9, T10, T11,
       T12, T13, T14, T15;

  not not_1 (not_1_out, DR_t);
  not not_2 (not_2_out, AC[15]);
  not not_3 (not_3_out, AC_t);
  not not_4 (not_4_out, E);
  not not_5 (not_5_out, I);
  not not_6 (not_6_out, R);
  and and_1 (r_t, D7, not_5_out, T3);
  Decoder #(.select(4)) decoder_1 (
    .out0(T0), .out1(T1), .out2(T2), .out3(T3), .out4(T4), .out5(T5), .out6(T6), .out7(T7), .out8(T8),
    .out9(T9), .out10(T10), .out11(T11), .out12(T12), .out13(T13), .out14(T14), .out15(T15), .sel(Seq),
    .en(1'b1));
  and and_2 (and_2_out, D4, T4);
  and and_3 (and_3_out, D5, T5);
  and and_4 (CLR, R, T1);
  and and_5 (and_5_out, not_6_out, T1);
  and and_6 (and_6_out, R, T2);
  and and_7 (and_7_out, D6, not_1_out, T6);
  and and_8 (and_8_out, r_t, not_2_out, IR[4]);
  and and_9 (and_9_out, r_t, AC[15], IR[3]);
  and and_10 (and_10_out, r_t, not_3_out, IR[2]);
  and and_11 (and_11_out, r_t, not_4_out, IR[1]);
  and and_12 (and_12_out, p, FGI, IR[9]);
  and and_13 (and_13_out, p, FGO, IR[8]);
  or or_1 (LD, and_2_out, and_3_out);
  or or_2 (INC, and_5_out, and_6_out, and_7_out, and_8_out, and_9_out, and_10_out, and_11_out, and_12_out, and_13_out);
  and and_14 (p, D7, I, T3);
  Decoder #(.select(3)) decoder_2 (
    .out0(D0), .out1(D1), .out2(D2), .out3(D3), .out4(D4), .out5(D5), .out6(D6), .out7(D7), .sel(IR[14:12]));  // open: en
  or or_3 (AC_t, AC[15], AC[14], AC[13], AC[12], AC[11], AC[10], AC[9], AC[8], AC[7], AC[6], AC[5], AC[4], AC[3], AC[2], AC[1], AC[0]);
  or or_4 (DR_t, DR[0], DR[1], DR[2], DR[3], DR[4], DR[5], DR[6], DR[7], DR[8], DR[9], DR[10], DR[11], DR[12], DR[13], DR[14], DR[15]);

  // Other names for the same wires on the sheet: AC_0 = AC[0]; AC_1 = AC[1]; AC_2 = AC[2]; AC_3 = AC[3]; AC_4 = AC[4];
  //   AC_5 = AC[5]; AC_6 = AC[6]; AC_7 = AC[7]; AC_8 = AC[8]; AC_9 = AC[9]; AC_10 = AC[10]; AC_11 = AC[11];
  //   AC_12 = AC[12]; AC_13 = AC[13]; AC_14 = AC[14]; AC_15 = AC[15]; B0 = IR[0]; B1 = IR[1]; B2 = IR[2]; B3 = IR[3];
  //   B4 = IR[4]; B5 = IR[5]; B6 = IR[6]; B7 = IR[7]; B8 = IR[8]; B9 = IR[9]; B10 = IR[10]; B11 = IR[11];
  //   IR_15 = IR[15]
endmodule

module DR (
  input  LD,
  input  [15:0] INPUT,
  input  INC,
  input  CLR,
  input  CLK,
  output [15:0] OUTPUT
);

  Counter #(.width(16), .max('hffff)) counter_1 (
    .load(LD), .D(INPUT), .count(INC), .Q(OUTPUT), .clk(CLK), .clr(CLR));  // open: carry
endmodule

module DR_Controller (
  input  [15:0] IR,
  input  [3:0] Seq,
  output LD,
  output INC
);

  wire and_1_out, and_2_out, and_3_out, and_4_out, D0, D1, D2, D3, D4, D5, D6, D7, T0, T1, T2, T3, T4, T5,
       T6, T7, T8, T9, T10, T11, T12, T13, T14, T15;

  Decoder #(.select(4)) decoder_1 (
    .out0(T0), .out1(T1), .out2(T2), .out3(T3), .out4(T4), .out5(T5), .out6(T6), .out7(T7), .out8(T8),
    .out9(T9), .out10(T10), .out11(T11), .out12(T12), .out13(T13), .out14(T14), .out15(T15), .sel(Seq),
    .en(1'b1));
  and and_1 (and_1_out, T4, D0);
  and and_2 (and_2_out, T4, D1);
  and and_3 (and_3_out, T4, D2);
  and and_4 (and_4_out, T4, D6);
  and and_5 (INC, D6, T5);
  or or_1 (LD, and_1_out, and_2_out, and_3_out, and_4_out);
  Decoder #(.select(3)) decoder_2 (
    .out0(D0), .out1(D1), .out2(D2), .out3(D3), .out4(D4), .out5(D5), .out6(D6), .out7(D7), .sel(IR[14:12]));  // open: en

  // Other names for the same wires on the sheet: B0 = IR[0]; B1 = IR[1]; B2 = IR[2]; B3 = IR[3]; B4 = IR[4];
  //   B5 = IR[5]; B6 = IR[6]; B7 = IR[7]; B8 = IR[8]; B9 = IR[9]; B10 = IR[10]; B11 = IR[11]; IR_15 = IR[15]
endmodule

module IR (
  input  LD,
  input  [15:0] INPUT,
  input  CLK,
  output [15:0] OUTPUT
);

  Counter #(.width(16), .max('hffff)) counter_1 (
    .load(LD), .D(INPUT), .count(1'b0), .Q(OUTPUT), .clk(CLK));  // open: carry, clr
endmodule

module IR_Controller (
  input  R,
  input  [3:0] Seq,
  output LD
);

  wire not_1_out, T0, T1, T2, T3, T4, T5, T6, T7, T8, T9, T10, T11, T12, T13, T14, T15;

  Decoder #(.select(4)) decoder_1 (
    .out0(T0), .out1(T1), .out2(T2), .out3(T3), .out4(T4), .out5(T5), .out6(T6), .out7(T7), .out8(T8),
    .out9(T9), .out10(T10), .out11(T11), .out12(T12), .out13(T13), .out14(T14), .out15(T15), .sel(Seq),
    .en(1'b1));
  not not_1 (not_1_out, R);
  and and_1 (LD, not_1_out, T1);
endmodule

module TR (
  input  LD,
  input  [15:0] INPUT,
  input  INC,
  input  CLR,
  input  CLK,
  output [15:0] OUTPUT
);

  Counter #(.width(16), .max('hffff)) counter_1 (
    .load(LD), .D(INPUT), .count(INC), .Q(OUTPUT), .clk(CLK), .clr(CLR));  // open: carry
endmodule

module TR_Controller (
  input  R,
  input  [3:0] Seq,
  output LD,
  output INC,
  output CLR
);

  wire T0, T1, T2, T3, T4, T5, T6, T7, T8, T9, T10, T11, T12, T13, T14, T15;

  and and_1 (LD, R, T0);
  Decoder #(.select(4)) decoder_1 (
    .out0(T0), .out1(T1), .out2(T2), .out3(T3), .out4(T4), .out5(T5), .out6(T6), .out7(T7), .out8(T8),
    .out9(T9), .out10(T10), .out11(T11), .out12(T12), .out13(T13), .out14(T14), .out15(T15), .sel(Seq),
    .en(1'b1));

  assign CLR = 1'b0;
  assign INC = 1'b0;
endmodule

module INPR (
  output [7:0] out_1
);

  Register register_1 (.en(1'b0), .Q(out_1));  // open: D, clk, clr
endmodule

module OUTR (
  input  [15:0] INPUT,
  input  LD,
  input  CLK,
  output [7:0] OUTPUT
);

  Counter counter_1 (.load(LD), .D(INPUT[7:0]), .count(1'b0), .Q(OUTPUT), .clk(CLK));  // open: carry, clr
endmodule

module OUTR_Controller (
  input  I,
  input  [15:0] IR,
  input  [3:0] Seq,
  output LD
);

  wire D0, D1, D2, D3, D4, D5, D6, D7, p, T0, T1, T2, T3, T4, T5, T6, T7, T8, T9, T10, T11, T12, T13, T14,
       T15;

  and and_1 (LD, p, IR[10]);
  and and_2 (p, D7, I, T3);
  Decoder #(.select(4)) decoder_1 (
    .out0(T0), .out1(T1), .out2(T2), .out3(T3), .out4(T4), .out5(T5), .out6(T6), .out7(T7), .out8(T8),
    .out9(T9), .out10(T10), .out11(T11), .out12(T12), .out13(T13), .out14(T14), .out15(T15), .sel(Seq),
    .en(1'b1));
  Decoder #(.select(3)) decoder_2 (
    .out0(D0), .out1(D1), .out2(D2), .out3(D3), .out4(D4), .out5(D5), .out6(D6), .out7(D7), .sel(IR[14:12]));  // open: en

  assign IR[15] = I;

  // Other names for the same wires on the sheet: B0 = IR[0]; B1 = IR[1]; B2 = IR[2]; B3 = IR[3]; B4 = IR[4];
  //   B5 = IR[5]; B6 = IR[6]; B7 = IR[7]; B8 = IR[8]; B9 = IR[9]; B10 = IR[10]; B11 = IR[11]; IR_15 = I
endmodule

module Memory (
  input  I,
  input  R,
  input  [15:0] IR,
  input  [3:0] Seq,
  output Write,
  output Read
);

  wire and_1_out, and_2_out, and_3_out, and_4_out, and_5_out, and_6_out, and_7_out, and_8_out, and_9_out,
       and_10_out, D0, D1, D2, D3, D4, D5, D6, D7, not_1_out, not_2_out, T0, T1, T2, T3, T4, T5, T6, T7, T8,
       T9, T10, T11, T12, T13, T14, T15;

  and and_1 (and_1_out, R, T1);
  and and_2 (and_2_out, D3, T4);
  or or_1 (Write, and_1_out, and_2_out, and_3_out, and_4_out);
  and and_3 (and_3_out, D5, T4);
  Decoder #(.select(4)) decoder_1 (
    .out0(T0), .out1(T1), .out2(T2), .out3(T3), .out4(T4), .out5(T5), .out6(T6), .out7(T7), .out8(T8),
    .out9(T9), .out10(T10), .out11(T11), .out12(T12), .out13(T13), .out14(T14), .out15(T15), .sel(Seq),
    .en(1'b1));
  and and_4 (and_4_out, D6, T6);
  and and_5 (and_5_out, not_1_out, T1);
  not not_1 (not_1_out, R);
  and and_6 (and_6_out, not_2_out, I, T3);
  not not_2 (not_2_out, D7);
  and and_7 (and_7_out, T4, D0);
  or or_2 (Read, and_5_out, and_6_out, and_7_out, and_8_out, and_9_out, and_10_out);
  Decoder #(.select(3)) decoder_2 (
    .out0(D0), .out1(D1), .out2(D2), .out3(D3), .out4(D4), .out5(D5), .out6(D6), .out7(D7), .sel(IR[14:12]));  // open: en
  and and_8 (and_8_out, T4, D1);
  and and_9 (and_9_out, T4, D2);
  and and_10 (and_10_out, T4, D6);

  // Other names for the same wires on the sheet: B0 = IR[0]; B1 = IR[1]; B2 = IR[2]; B3 = IR[3]; B4 = IR[4];
  //   B5 = IR[5]; B6 = IR[6]; B7 = IR[7]; B8 = IR[8]; B9 = IR[9]; B10 = IR[10]; B11 = IR[11]; IR_15 = IR[15]
endmodule

// SC
module SC_Clear_Controller (
  input  I,
  input  R,
  input  [15:0] IR,
  input  [3:0] Seq,
  output SC_CLR
);

  wire and_1_out, and_2_out, and_3_out, and_4_out, and_5_out, and_6_out, and_7_out, and_8_out, D0, D1, D2,
       D3, D4, D5, D6, D7, not_1_out, p, r_t, T0, T1, T2, T3, T4, T5, T6, T7, T8, T9, T10, T11, T12, T13,
       T14, T15;

  and and_1 (and_1_out, R, T2);
  and and_2 (and_2_out, D0, T5);
  and and_3 (and_3_out, D1, T5);
  and and_4 (and_4_out, D2, T5);
  and and_5 (and_5_out, D5, T5);
  and and_6 (and_6_out, D3, T4);
  and and_7 (and_7_out, D4, T4);
  and and_8 (and_8_out, D6, T6);
  not not_1 (not_1_out, I);
  Decoder #(.select(4)) decoder_1 (
    .out0(T0), .out1(T1), .out2(T2), .out3(T3), .out4(T4), .out5(T5), .out6(T6), .out7(T7), .out8(T8),
    .out9(T9), .out10(T10), .out11(T11), .out12(T12), .out13(T13), .out14(T14), .out15(T15), .sel(Seq),
    .en(1'b1));
  and and_9 (r_t, D7, not_1_out, T3);
  or or_1 (SC_CLR, and_1_out, and_2_out, and_3_out, and_4_out, and_5_out, and_6_out, and_7_out, and_8_out, r_t, p);
  and and_10 (p, D7, I, T3);
  Decoder #(.select(3)) decoder_2 (
    .out0(D0), .out1(D1), .out2(D2), .out3(D3), .out4(D4), .out5(D5), .out6(D6), .out7(D7), .sel(IR[14:12]));  // open: en

  // Other names for the same wires on the sheet: B0 = IR[0]; B1 = IR[1]; B2 = IR[2]; B3 = IR[3]; B4 = IR[4];
  //   B5 = IR[5]; B6 = IR[6]; B7 = IR[7]; B8 = IR[8]; B9 = IR[9]; B10 = IR[10]; B11 = IR[11]; IR_15 = IR[15]
endmodule

// R
module R_Controller (
  input  CLK,
  input  IEN,
  input  FGO,
  input  FGI,
  input  [3:0] Seq,
  output R
);

  wire and_1_out, and_2_out, not_1_out, not_2_out, not_3_out, or_1_out, T0, T1, T2, T3, T4, T5, T6, T7, T8,
       T9, T10, T11, T12, T13, T14, T15;

  not not_1 (not_1_out, T0);
  not not_2 (not_2_out, T1);
  not not_3 (not_3_out, T2);
  or or_1 (or_1_out, FGI, FGO);
  and and_1 (and_1_out, R, T2);
  Decoder #(.select(4)) decoder_1 (
    .out0(T0), .out1(T1), .out2(T2), .out3(T3), .out4(T4), .out5(T5), .out6(T6), .out7(T7), .out8(T8),
    .out9(T9), .out10(T10), .out11(T11), .out12(T12), .out13(T13), .out14(T14), .out15(T15), .sel(Seq),
    .en(1'b1));
  and and_2 (and_2_out, not_1_out, not_2_out, not_3_out, IEN, or_1_out);
  J_K_Flip_Flop j_k_ff_1 (.J(and_2_out), .clk(CLK), .K(and_1_out), .Q(R));  // open: Qn, preset, en, reset
endmodule

// I
module I_Controller (
  input  CLK,
  input  IR_15,
  input  R,
  input  [3:0] Seq,
  output I
);

  wire and_1_out, not_1_out, T0, T1, T2, T3, T4, T5, T6, T7, T8, T9, T10, T11, T12, T13, T14, T15;

  not not_1 (not_1_out, R);
  Decoder #(.select(4)) decoder_1 (
    .out0(T0), .out1(T1), .out2(T2), .out3(T3), .out4(T4), .out5(T5), .out6(T6), .out7(T7), .out8(T8),
    .out9(T9), .out10(T10), .out11(T11), .out12(T12), .out13(T13), .out14(T14), .out15(T15), .sel(Seq),
    .en(1'b1));
  and and_1 (and_1_out, not_1_out, T2);
  D_Flip_Flop d_ff_1 (.clk(CLK), .D(IR_15), .Q(I), .en(and_1_out));  // open: Qn, preset, reset
endmodule

// S
module S_Controller (
  input  CLK,
  input  I,
  input  [15:0] IR,
  input  [3:0] Seq,
  output S
);

  wire and_1_out, D0, D1, D2, D3, D4, D5, D6, D7, not_1_out, r, T0, T1, T2, T3, T4, T5, T6, T7, T8, T9, T10,
       T11, T12, T13, T14, T15;

  and and_1 (and_1_out, r, IR[0]);
  not not_1 (not_1_out, I);
  Decoder #(.select(4)) decoder_1 (
    .out0(T0), .out1(T1), .out2(T2), .out3(T3), .out4(T4), .out5(T5), .out6(T6), .out7(T7), .out8(T8),
    .out9(T9), .out10(T10), .out11(T11), .out12(T12), .out13(T13), .out14(T14), .out15(T15), .sel(Seq),
    .en(1'b1));
  and and_2 (r, D7, not_1_out, T3);
  J_K_Flip_Flop j_k_ff_1 (.J(and_1_out), .clk(CLK), .K(1'b0), .Q(S));  // open: Qn, preset, en, reset
  Decoder #(.select(3)) decoder_2 (
    .out0(D0), .out1(D1), .out2(D2), .out3(D3), .out4(D4), .out5(D5), .out6(D6), .out7(D7), .sel(IR[14:12]));  // open: en

  // Other names for the same wires on the sheet: B0 = IR[0]; B1 = IR[1]; B2 = IR[2]; B3 = IR[3]; B4 = IR[4];
  //   B5 = IR[5]; B6 = IR[6]; B7 = IR[7]; B8 = IR[8]; B9 = IR[9]; B10 = IR[10]; B11 = IR[11]; IR_15 = IR[15]
endmodule

// IEN
module IEN_Controller (
  input  CLK,
  input  I,
  input  R,
  input  [15:0] IR,
  input  [3:0] Seq,
  output IEN
);

  wire and_1_out, and_2_out, and_3_out, D0, D1, D2, D3, D4, D5, D6, D7, or_1_out, p, T0, T1, T2, T3, T4, T5,
       T6, T7, T8, T9, T10, T11, T12, T13, T14, T15;

  and and_1 (and_1_out, p, IR[7]);
  and and_2 (and_2_out, R, T2);
  and and_3 (and_3_out, p, IR[6]);
  and and_4 (p, D7, I, T3);
  Decoder #(.select(4)) decoder_1 (
    .out0(T0), .out1(T1), .out2(T2), .out3(T3), .out4(T4), .out5(T5), .out6(T6), .out7(T7), .out8(T8),
    .out9(T9), .out10(T10), .out11(T11), .out12(T12), .out13(T13), .out14(T14), .out15(T15), .sel(Seq),
    .en(1'b1));
  or or_1 (or_1_out, and_2_out, and_3_out);
  J_K_Flip_Flop j_k_ff_1 (.J(and_1_out), .clk(CLK), .K(or_1_out), .Q(IEN));  // open: Qn, preset, en, reset
  Decoder #(.select(3)) decoder_2 (
    .out0(D0), .out1(D1), .out2(D2), .out3(D3), .out4(D4), .out5(D5), .out6(D6), .out7(D7), .sel(IR[14:12]));  // open: en

  // Other names for the same wires on the sheet: B0 = IR[0]; B1 = IR[1]; B2 = IR[2]; B3 = IR[3]; B4 = IR[4];
  //   B5 = IR[5]; B6 = IR[6]; B7 = IR[7]; B8 = IR[8]; B9 = IR[9]; B10 = IR[10]; B11 = IR[11]; IR_15 = IR[15]
endmodule

// FGO
module FGO_Controller (
  input  CLK,
  input  I,
  input  [15:0] IR,
  input  [3:0] Seq,
  output FGO
);

  wire and_2_out, D0, D1, D2, D3, D4, D5, D6, D7, p, T0, T1, T2, T3, T4, T5, T6, T7, T8, T9, T10, T11, T12,
       T13, T14, T15;

  and and_1 (p, D7, I, T3);
  Decoder #(.select(4)) decoder_1 (
    .out0(T0), .out1(T1), .out2(T2), .out3(T3), .out4(T4), .out5(T5), .out6(T6), .out7(T7), .out8(T8),
    .out9(T9), .out10(T10), .out11(T11), .out12(T12), .out13(T13), .out14(T14), .out15(T15), .sel(Seq),
    .en(1'b1));
  and and_2 (and_2_out, p, IR[10]);
  J_K_Flip_Flop j_k_ff_1 (.J(1'b0), .clk(CLK), .K(and_2_out), .Q(FGO));  // open: Qn, preset, en, reset
  Decoder #(.select(3)) decoder_2 (
    .out0(D0), .out1(D1), .out2(D2), .out3(D3), .out4(D4), .out5(D5), .out6(D6), .out7(D7), .sel(IR[14:12]));  // open: en

  // Other names for the same wires on the sheet: B0 = IR[0]; B1 = IR[1]; B2 = IR[2]; B3 = IR[3]; B4 = IR[4];
  //   B5 = IR[5]; B6 = IR[6]; B7 = IR[7]; B8 = IR[8]; B9 = IR[9]; B10 = IR[10]; B11 = IR[11]; IR_15 = IR[15]
endmodule

// FGI
module FGI_Controller (
  input  [7:0] INPUT,
  input  CLK,
  input  I,
  input  [15:0] IR,
  input  [3:0] Seq,
  output FGI
);

  wire and_1_out, D0, D1, D2, D3, D4, D5, D6, D7, INPR, p, T0, T1, T2, T3, T4, T5, T6, T7, T8, T9, T10, T11,
       T12, T13, T14, T15;

  and and_1 (and_1_out, p, IR[11]);
  and and_2 (p, D7, I, T3);
  Decoder #(.select(4)) decoder_1 (
    .out0(T0), .out1(T1), .out2(T2), .out3(T3), .out4(T4), .out5(T5), .out6(T6), .out7(T7), .out8(T8),
    .out9(T9), .out10(T10), .out11(T11), .out12(T12), .out13(T13), .out14(T14), .out15(T15), .sel(Seq),
    .en(1'b1));
  J_K_Flip_Flop j_k_ff_1 (.J(INPR), .clk(CLK), .K(and_1_out), .Q(FGI));  // open: Qn, preset, en, reset
  Decoder #(.select(3)) decoder_2 (
    .out0(D0), .out1(D1), .out2(D2), .out3(D3), .out4(D4), .out5(D5), .out6(D6), .out7(D7), .sel(IR[14:12]));  // open: en
  or or_1 (INPR, INPUT[0], INPUT[1], INPUT[2], INPUT[3], INPUT[4], INPUT[5], INPUT[6], INPUT[7]);

  // Other names for the same wires on the sheet: B0 = IR[0]; B1 = IR[1]; B2 = IR[2]; B3 = IR[3]; B4 = IR[4];
  //   B5 = IR[5]; B6 = IR[6]; B7 = IR[7]; B8 = IR[8]; B9 = IR[9]; B10 = IR[10]; B11 = IR[11]; IR_15 = IR[15]
endmodule

module BUS_Controller (
  input  I,
  input  R,
  input  [15:0] IR,
  input  [3:0] Seq,
  output [2:0] SELECT
);

  wire and_1_out, and_2_out, and_3_out, and_4_out, and_5_out, and_6_out, and_7_out, and_8_out, and_9_out,
       and_10_out, and_12_out, and_13_out, and_14_out, and_17_out, and_18_out, D0, D1, D2, D3, D4, D5, D6,
       D7, not_1_out, not_2_out, not_3_out, not_4_out, not_5_out, p, r_t, T0, T1, T2, T3, T4, T5, T6, T7, T8,
       T9, T10, T11, T12, T13, T14, T15, x1, x2, x3, x4, x5, x6, x7;

  not not_1 (not_1_out, R);
  not not_2 (not_2_out, D7);
  and and_1 (and_1_out, D4, T4);
  and and_2 (and_2_out, D5, T5);
  and and_3 (and_3_out, D3, T4);
  and and_4 (and_4_out, p, IR[10]);
  and and_5 (and_5_out, not_1_out, T1);
  and and_6 (and_6_out, D0, T4);
  and and_7 (and_7_out, D1, T4);
  and and_8 (and_8_out, D2, T4);
  and and_9 (and_9_out, D6, T4);
  and and_10 (and_10_out, not_2_out, I, T3);
  not not_3 (not_3_out, I);
  Priority_Encoder priority_encoder_1 (
    .in0(1'b0), .in1(x1), .in2(x2), .in3(x3), .in4(x4), .in5(x5), .in6(x6), .in7(x7), .out(SELECT));  // open: en_in, gs, en_out
  or or_1 (x1, and_1_out, and_2_out);
  and and_11 (r_t, D7, not_3_out, T3);
  Decoder #(.select(4)) decoder_1 (
    .out0(T0), .out1(T1), .out2(T2), .out3(T3), .out4(T4), .out5(T5), .out6(T6), .out7(T7), .out8(T8),
    .out9(T9), .out10(T10), .out11(T11), .out12(T12), .out13(T13), .out14(T14), .out15(T15), .sel(Seq),
    .en(1'b1));
  or or_2 (x4, and_3_out, and_4_out);
  or or_3 (x7, and_5_out, and_6_out, and_7_out, and_8_out, and_9_out, and_10_out);
  not not_4 (not_4_out, R);
  and and_12 (and_12_out, not_4_out, T0);
  and and_13 (and_13_out, R, T0);
  and and_14 (and_14_out, D5, T4);
  and and_15 (p, D7, I, T3);
  not not_5 (not_5_out, R);
  Decoder #(.select(3)) decoder_2 (
    .out0(D0), .out1(D1), .out2(D2), .out3(D3), .out4(D4), .out5(D5), .out6(D6), .out7(D7), .sel(IR[14:12]));  // open: en
  or or_4 (x2, and_12_out, and_13_out, and_14_out);
  and and_16 (x5, not_5_out, T2);
  and and_17 (and_17_out, D2, T5);
  and and_18 (and_18_out, D6, T6);
  and and_19 (x6, R, T1);
  or or_5 (x3, and_17_out, and_18_out);

  // Other names for the same wires on the sheet: B0 = IR[0]; B1 = IR[1]; B2 = IR[2]; B3 = IR[3]; B4 = IR[4];
  //   B5 = IR[5]; B6 = IR[6]; B7 = IR[7]; B8 = IR[8]; B9 = IR[9]; B10 = IR[10]; B11 = IR[11]; IR_15 = IR[15]
endmodule

// E
module E_Controller (
  input  in_1,
  input  E_out,
  input  I,
  input  [15:0] IR,
  input  [3:0] Seq,
  input  [15:0] AC,
  output E
);

  wire and_1_out, and_2_out, and_3_out, and_4_out, and_5_out, and_6_out, and_7_out, and_8_out, and_9_out, D0,
       D1, D2, D3, D4, D5, D6, D7, not_1_out, not_2_out, not_3_out, r, RESET_out, SET_out, T0, T1, T2, T3,
       T4, T5, T6, T7, T8, T9, T10, T11, T12, T13, T14, T15;

  not not_1 (not_1_out, AC[0]);
  not not_2 (not_2_out, AC[15]);
  not not_3 (not_3_out, I);
  Decoder #(.select(4)) decoder_1 (
    .out0(T0), .out1(T1), .out2(T2), .out3(T3), .out4(T4), .out5(T5), .out6(T6), .out7(T7), .out8(T8),
    .out9(T9), .out10(T10), .out11(T11), .out12(T12), .out13(T13), .out14(T14), .out15(T15), .sel(Seq),
    .en(1'b1));
  and and_1 (and_1_out, r, IR[8]);
  and and_2 (and_2_out, D1, T5, E_out);
  and and_3 (and_3_out, r, IR[6], AC[15]);
  and and_4 (and_4_out, r, IR[7], AC[0]);
  and and_5 (and_5_out, r, IR[8]);
  and and_6 (and_6_out, r, IR[6], not_1_out);
  and and_7 (and_7_out, D1, T5, E_out);
  and and_8 (and_8_out, r, IR[7], not_2_out);
  and and_9 (and_9_out, r, IR[10]);
  and and_10 (r, D7, not_3_out, T3);
  or SET (SET_out, and_1_out, and_2_out, and_3_out, and_4_out);
  or RESET (RESET_out, and_5_out, and_6_out, and_7_out, and_8_out, and_9_out);
  J_K_Flip_Flop j_k_ff_1 (.J(SET_out), .clk(in_1), .K(RESET_out), .Q(E));  // open: Qn, preset, en, reset
  Decoder #(.select(3)) decoder_2 (
    .out0(D0), .out1(D1), .out2(D2), .out3(D3), .out4(D4), .out5(D5), .out6(D6), .out7(D7), .sel(IR[14:12]));  // open: en

  // Other names for the same wires on the sheet: AC_0 = AC[0]; AC_1 = AC[1]; AC_2 = AC[2]; AC_3 = AC[3]; AC_4 = AC[4];
  //   AC_5 = AC[5]; AC_6 = AC[6]; AC_7 = AC[7]; AC_8 = AC[8]; AC_9 = AC[9]; AC_10 = AC[10]; AC_11 = AC[11];
  //   AC_12 = AC[12]; AC_13 = AC[13]; AC_14 = AC[14]; AC_15 = AC[15]; B0 = IR[0]; B1 = IR[1]; B2 = IR[2]; B3 = IR[3];
  //   B4 = IR[4]; B5 = IR[5]; B6 = IR[6]; B7 = IR[7]; B8 = IR[8]; B9 = IR[9]; B10 = IR[10]; B11 = IR[11];
  //   IR_15 = IR[15]
endmodule
